// Logisim project 3bit_greycode_D_FF.circ as structural Verilog: 1 circuit, main circuit main
module main (
  output out_1,
  output out_2,
  output out_3
);

  wire and_1_out, and_2_out, and_3_out, and_4_out, and_5_out, and_6_out, clock_1_out, d_ff_1_qn, d_ff_2_qn,
       d_ff_3_qn, or_1_out, or_2_out, or_3_out;

  and and_1 (and_1_out, out_2, d_ff_3_qn);
  and and_2 (and_2_out, out_1, out_3);
  Clock clock_1 (.out(clock_1_out));
  or or_1 (or_1_out, and_1_out, and_2_out);
  and and_3 (and_3_out, d_ff_3_qn, out_2);
  and and_4 (and_4_out, d_ff_1_qn, out_3);
  D_Flip_Flop d_ff_1 (.clk(clock_1_out), .D(or_1_out), .Q(out_1), .Qn(d_ff_1_qn));  // open: preset, en, reset
  or or_2 (or_2_out, and_3_out, and_4_out);
  D_Flip_Flop d_ff_2 (.clk(clock_1_out), .D(or_2_out), .Q(out_2), .Qn(d_ff_2_qn));  // open: preset, en, reset
  and and_5 (and_5_out, d_ff_1_qn, d_ff_2_qn);
  and and_6 (and_6_out, out_1, out_2);
  or or_3 (or_3_out, and_5_out, and_6_out);
  D_Flip_Flop d_ff_3 (.clk(clock_1_out), .D(or_3_out), .Q(out_3), .Qn(d_ff_3_qn));  // open: preset, en, reset
endmodule
