// Logisim project 3bit_greycode_JK_FF.circ as structural Verilog: 1 circuit, main circuit main
module main (
  output out_1,
  output out_2,
  output out_3
);

  wire and_1_out, and_2_out, and_3_out, and_4_out, and_5_out, and_6_out, and_7_out, and_8_out, clock_1_out,
       j_k_ff_1_qn, j_k_ff_2_qn, j_k_ff_3_qn, or_1_out, or_2_out;

  and and_1 (and_1_out, j_k_ff_3_qn, out_2);
  and and_2 (and_2_out, j_k_ff_2_qn, j_k_ff_3_qn);
  Clock clock_1 (.out(clock_1_out));
  J_K_Flip_Flop j_k_ff_1 (
    .J(and_1_out), .clk(clock_1_out), .K(and_2_out), .Q(out_1), .Qn(j_k_ff_1_qn));  // open: preset, en, reset
  and and_3 (and_3_out, j_k_ff_1_qn, out_3);
  and and_4 (and_4_out, out_1, out_3);
  J_K_Flip_Flop j_k_ff_2 (
    .J(and_3_out), .clk(clock_1_out), .K(and_4_out), .Q(out_2), .Qn(j_k_ff_2_qn));  // open: preset, en, reset
  and and_5 (and_5_out, j_k_ff_1_qn, j_k_ff_2_qn);
  and and_6 (and_6_out, out_2, out_1);
  and and_7 (and_7_out, j_k_ff_1_qn, out_2);
  and and_8 (and_8_out, out_1, j_k_ff_2_qn);
  or or_1 (or_1_out, and_5_out, and_6_out);
  or or_2 (or_2_out, and_7_out, and_8_out);
  J_K_Flip_Flop j_k_ff_3 (
    .J(or_1_out), .clk(clock_1_out), .K(or_2_out), .Q(out_3), .Qn(j_k_ff_3_qn));  // open: preset, en, reset
endmodule
