// Logisim project 4bit_DFF_counter.circ as structural Verilog: 1 circuit, main circuit main
module main (
  input  CLK,
  input  CLR,
  output Q0,
  output Q1,
  output Q2,
  output Q3
);

  wire FF0_qn, FF1_qn, FF2_qn, FF3_qn;

  D_Flip_Flop FF0 (.clk(CLK), .D(FF0_qn), .Q(Q0), .Qn(FF0_qn), .preset(CLR), .en(CLR), .reset(CLR));
  D_Flip_Flop FF1 (.clk(Q0), .D(FF1_qn), .Qn(FF1_qn), .preset(CLR), .en(CLR), .reset(CLR));  // open: Q
  D_Flip_Flop FF2 (.clk(Q0), .D(FF2_qn), .Qn(FF2_qn), .preset(CLR), .en(CLR), .reset(CLR));  // open: Q
  D_Flip_Flop FF3 (.clk(Q0), .D(FF3_qn), .Qn(FF3_qn), .preset(CLR), .en(CLR), .reset(CLR));  // open: Q

  assign Q1 = Q0;
  assign Q2 = Q0;
  assign Q3 = Q0;

  // Notes on the sheet:
  //   4-bit Asynchronous (Ripple) Counter using D Flip-Flops
  //   Each D-FF is wired as a Toggle FF (D tied to Q'). Q of each stage clocks the next stage.
endmodule
