// Logisim project 4bit_register.circ as structural Verilog: 1 circuit, main circuit 4 bit Register
module _4_bit_Register (
  input  D0,
  input  D1,
  input  D2,
  input  D3,
  input  CLK,
  input  CLR,
  output Q0,
  output Q1,
  output Q2,
  output Q3
);

  D_Flip_Flop FF0 (.clk(CLK), .D(D0), .Q(Q0), .preset(CLR), .en(CLR), .reset(CLR));  // open: Qn
  D_Flip_Flop FF1 (.clk(CLK), .D(D1), .Q(Q1), .preset(CLR), .en(CLR), .reset(CLR));  // open: Qn
  D_Flip_Flop FF2 (.clk(CLK), .D(D2), .Q(Q2), .preset(CLR), .en(CLR), .reset(CLR));  // open: Qn
  D_Flip_Flop FF3 (.clk(CLK), .D(D3), .Q(Q3), .preset(CLR), .en(CLR), .reset(CLR));  // open: Qn

  // Notes on the sheet:
  //   4-bit Register using D Flip-Flops
endmodule
