// Logisim project WEEK2 CIRCUITS.circ as structural Verilog: 12 circuits, main circuit Half Adder
module Half_Adder (
  input  x,
  input  y,
  output sum,
  output carry
);

  and and_1 (sum, x, y);
  xor xor_1 (carry, x, y);
endmodule

module Full_Adder (
  input  x,
  input  y,
  input  z,
  output sum,
  output carry
);

  wire and_1_out, and_2_out, and_3_out, and_4_out, and_5_out, and_6_out, and_7_out, not_1_out, not_2_out,
       not_3_out, not_4_out, not_5_out, not_6_out;

  and and_1 (and_1_out, y, z);
  and and_2 (and_2_out, x, z);
  and and_3 (and_3_out, x, y);
  not not_1 (not_1_out, x);
  and and_4 (and_4_out, not_1_out, not_2_out, z);
  not not_2 (not_2_out, y);
  not not_3 (not_3_out, x);
  and and_5 (and_5_out, not_3_out, y, not_4_out);
  not not_4 (not_4_out, z);
  and and_6 (and_6_out, x, not_5_out, not_6_out);
  not not_5 (not_5_out, y);
  not not_6 (not_6_out, z);
  and and_7 (and_7_out, x, y, z);
  or or_1 (sum, and_1_out, and_2_out, and_3_out);
  or or_2 (carry, and_4_out, and_5_out, and_6_out, and_7_out);
endmodule

module Half_Subtracor (
  input  a,
  input  b,
  output difference,
  output borrow
);

  wire and_1_out, and_2_out, not_1_out, not_2_out, not_3_out;

  not not_1 (not_1_out, a);
  not not_2 (not_2_out, b);
  not not_3 (not_3_out, a);
  and and_1 (and_1_out, not_1_out, b);
  and and_2 (and_2_out, a, not_2_out);
  and and_3 (borrow, not_3_out, b);
  or or_1 (difference, and_1_out, and_2_out);
endmodule

module Full_Adder_2_Half (
  input  in_1,
  input  in_2,
  input  in_3,
  output out_4,
  output out_5
);

  wire half_adder_1_carry, half_adder_1_sum, half_adder_2_sum;

  Half_Adder half_adder_1 (.x(in_1), .y(in_2), .carry(half_adder_1_carry), .sum(half_adder_1_sum));
  Half_Adder half_adder_2 (.x(half_adder_1_carry), .y(in_3), .carry(out_4), .sum(half_adder_2_sum));
  or or_1 (out_5, half_adder_2_sum, half_adder_1_sum);
endmodule

module Full_Subtractor (
  input  in_1,
  input  in_2,
  input  in_3,
  output out_4,
  output out_5
);

  wire adder_1_cout, not_1_out;

  not not_1 (not_1_out, in_3);
  Adder #(.width(1)) adder_1 (.a(in_2), .b(not_1_out), .out(out_4), .cin(in_1), .cout(adder_1_cout));
  not not_2 (out_5, adder_1_cout);
endmodule

module _4_Bit_Ripple_Carry_Adder (
  input  in_1,
  input  in_2,
  input  in_3,
  input  in_4,
  input  in_5,
  input  in_6,
  input  in_7,
  input  in_8,
  input  in_9,
  output out_10,
  output out_11,
  output out_12,
  output out_13,
  output out_14
);

  wire adder_2_cout, adder_3_cout, adder_4_cout;

  Adder #(.width(1)) adder_1 (.a(in_8), .b(in_7), .out(out_11), .cin(adder_2_cout), .cout(out_10));
  Adder #(.width(1)) adder_2 (.a(in_2), .b(in_1), .out(out_13), .cin(adder_3_cout), .cout(adder_2_cout));
  Adder #(.width(1)) adder_3 (.a(in_4), .b(in_3), .out(out_14), .cin(adder_4_cout), .cout(adder_3_cout));
  Adder #(.width(1)) adder_4 (.a(in_6), .b(in_5), .out(out_12), .cin(in_9), .cout(adder_4_cout));
endmodule

module ALU (
  input  in_1,
  input  in_2,
  input  [1:0] in_3,
  input  in_4,
  output out_5
);

  wire adder_1_out, and_1_out, or_1_out, subtractor_1_out;

  or or_1 (or_1_out, in_1, in_2);
  and and_1 (and_1_out, in_1, in_2);
  Adder #(.width(1)) adder_1 (.a(in_1), .b(in_2), .out(adder_1_out), .cin(1'b1));  // open: cout
  Subtractor #(.width(1)) subtractor_1 (.a(in_1), .b(in_2), .out(subtractor_1_out), .bin(1'b1));  // open: bout
  Multiplexer #(.select(2)) multiplexer_1 (
    .in0(or_1_out), .in1(and_1_out), .in2(adder_1_out), .in3(subtractor_1_out), .out(out_5), .sel(in_3),
    .en(in_4));
endmodule

module Full_Adder_using_Basic_Gates (
  input  A,
  input  B,
  input  Cin,
  output S,
  output C
);

  wire and_1_out, and_2_out, and_3_out, xor_1_out;

  xor xor_1 (xor_1_out, A, B);
  and and_1 (and_1_out, A, B);
  and and_2 (and_2_out, A, Cin);
  and and_3 (and_3_out, B, Cin);
  xor xor_2 (S, xor_1_out, Cin);
  or or_1 (C, and_1_out, and_2_out, and_3_out);

  // Notes on the sheet:
  //   Using Basic Gates
endmodule

module challenge_activity1 (
  input  p2,
  input  p3,
  input  p1,
  input  p2_2,
  input  p3_2,
  output Y,
  output Z
);

  wire and_1_out, and_2_out, not_1_out, not_2_out;

  not not_1 (not_1_out, p3);
  not not_2 (not_2_out, p2_2);
  and and_1 (and_1_out, p2, not_1_out);
  and and_2 (and_2_out, p1, not_2_out);
  or or_1 (Y, and_1_out, p3);
  or or_2 (Z, and_2_out, p3_2);

  // Notes on the sheet:
  //   cct to control priority level of printing jobs
endmodule

module challenge_activty_2 (
  input  S1,
  input  S2,
  input  S3,
  input  S1_2,
  input  S2_2,
  input  S3_2,
  input  S1_3,
  input  S2_3,
  input  S3_3,
  output ARM_1,
  output ARM_2,
  output ARM_3
);

  wire not_1_out, not_2_out, not_3_out;

  not not_1 (not_1_out, S3);
  not not_2 (not_2_out, S2_3);
  not not_3 (not_3_out, S3_3);
  and and_1 (ARM_1, S1, S2, not_1_out);
  and and_2 (ARM_2, S1_2, S2_2, S3_2);
  and and_3 (ARM_3, S1_3, not_2_out, not_3_out);

  // Notes on the sheet:
  //   process line control problem
endmodule

module CHALLENGE_ACTIVITY_3 (
  input  A,
  input  B,
  input  C,
  input  D,
  output out_5
);

  wire and_1_out, and_2_out, and_3_out, not_1_out, not_2_out;

  not not_1 (not_1_out, A);
  not not_2 (not_2_out, B);
  and and_1 (and_1_out, not_1_out, C);
  and and_2 (and_2_out, not_2_out, C, D);
  and and_3 (and_3_out, not_1_out, not_2_out, D);
  or or_1 (out_5, and_1_out, and_2_out, and_3_out);

  // Notes on the sheet:
  //   cct able to compare magnitude of two bit binary num AB and CD
endmodule

module CHALLENGE_ACTIVITY_4 (
  input  IGNITION,
  input  ENGINE_TEMP_S2,
  input  in_3,
  input  IGNITION_2,
  input  ENGINE_TEMP_S2_2,
  input  ENGINE_OIL__S3,
  output ENGINE,
  output FA,
  output OA
);

  wire and_1_out, and_2_out, not_1_out, not_2_out, not_3_out, not_4_out, not_5_out, not_6_out;

  not not_1 (not_1_out, ENGINE_TEMP_S2);
  not not_2 (not_2_out, in_3);
  not not_3 (not_3_out, ENGINE_TEMP_S2_2);
  not not_4 (not_4_out, ENGINE_OIL__S3);
  not not_5 (not_5_out, IGNITION_2);
  and and_1 (and_1_out, IGNITION, not_1_out, not_2_out);
  not not_6 (not_6_out, IGNITION);
  and and_2 (and_2_out, not_6_out, not_1_out, in_3);
  and and_3 (FA, IGNITION_2, not_3_out, not_4_out);
  and and_4 (OA, not_5_out, ENGINE_TEMP_S2_2, ENGINE_OIL__S3);
  or or_1 (ENGINE, and_1_out, and_2_out);

  // Notes on the sheet:
  //   ENGINE OIL (S3)
endmodule
