// Logisim project week 4 circuits.circ as structural Verilog: 4 circuits, main circuit  synchronous BCD decade counter
module synchronous_BCD_decade_counter (
  input  in_1
);

  wire and_1_out, and_2_out, and_3_out, and_4_out, clock_1_out, j_k_ff_1_q, j_k_ff_2_q, j_k_ff_3_q,
       j_k_ff_4_q, j_k_ff_4_qn, or_1_out;

  Clock clock_1 (.out(clock_1_out));
  J_K_Flip_Flop j_k_ff_1 (.J(in_1), .clk(clock_1_out), .K(in_1), .Q(j_k_ff_1_q));  // open: Qn, preset, en, reset
  and and_1 (and_1_out, j_k_ff_1_q, j_k_ff_4_qn);
  J_K_Flip_Flop j_k_ff_2 (
    .J(and_1_out), .clk(clock_1_out), .K(and_1_out), .Q(j_k_ff_2_q));  // open: Qn, preset, en, reset
  and and_2 (and_2_out, j_k_ff_1_q, j_k_ff_2_q);
  J_K_Flip_Flop j_k_ff_3 (
    .J(and_2_out), .clk(clock_1_out), .K(and_2_out), .Q(j_k_ff_3_q));  // open: Qn, preset, en, reset
  and and_3 (and_3_out, j_k_ff_4_q, j_k_ff_1_q);
  and and_4 (and_4_out, and_2_out, j_k_ff_3_q);
  J_K_Flip_Flop j_k_ff_4 (
    .J(or_1_out), .clk(clock_1_out), .K(or_1_out), .Q(j_k_ff_4_q), .Qn(j_k_ff_4_qn));  // open: preset, en, reset
  or or_1 (or_1_out, and_3_out, and_4_out);
endmodule

module counter_decoding (
  input  in_1,
  output out_2
);

  wire and_1_out, clock_1_out, j_k_ff_1_q, j_k_ff_1_qn, j_k_ff_2_q, j_k_ff_3_q;

  Clock clock_1 (.out(clock_1_out));
  J_K_Flip_Flop j_k_ff_1 (
    .J(in_1), .clk(clock_1_out), .K(in_1), .Q(j_k_ff_1_q), .Qn(j_k_ff_1_qn));  // open: preset, en, reset
  J_K_Flip_Flop j_k_ff_2 (
    .J(j_k_ff_1_q), .clk(clock_1_out), .K(j_k_ff_1_q), .Q(j_k_ff_2_q));  // open: Qn, preset, en, reset
  and and_1 (and_1_out, j_k_ff_1_q, j_k_ff_2_q);
  and and_2 (out_2, j_k_ff_1_qn, j_k_ff_2_q, j_k_ff_3_q);
  J_K_Flip_Flop j_k_ff_3 (
    .J(and_1_out), .clk(clock_1_out), .K(and_1_out), .Q(j_k_ff_3_q));  // open: Qn, preset, en, reset
endmodule

module A_3_bit_counter_with_active_HIGH_decoding_of_count_2_and_count_7 (
  input  in_1,
  output out_2,
  output out_3
);

  wire and_2_out, clock_1_out, j_k_ff_1_q, j_k_ff_1_qn, j_k_ff_2_q, j_k_ff_3_q, j_k_ff_3_qn;

  Clock clock_1 (.out(clock_1_out));
  J_K_Flip_Flop j_k_ff_1 (
    .J(in_1), .clk(clock_1_out), .K(in_1), .Q(j_k_ff_1_q), .Qn(j_k_ff_1_qn));  // open: preset, en, reset
  J_K_Flip_Flop j_k_ff_2 (
    .J(j_k_ff_1_q), .clk(clock_1_out), .K(j_k_ff_1_q), .Q(j_k_ff_2_q));  // open: Qn, preset, en, reset
  and and_1 (out_3, j_k_ff_1_qn, j_k_ff_2_q, j_k_ff_3_qn);
  and and_2 (and_2_out, j_k_ff_1_q, j_k_ff_2_q);
  J_K_Flip_Flop j_k_ff_3 (
    .J(and_2_out), .clk(clock_1_out), .K(and_2_out), .Q(j_k_ff_3_q), .Qn(j_k_ff_3_qn));  // open: preset, en, reset
  and and_3 (out_2, j_k_ff_2_q, j_k_ff_1_q, j_k_ff_3_q);
endmodule

module digital_clock (
  input  in_1
);

  wire and_1_out, and_2_out, and_3_out, and_4_out, and_5_out, and_6_out, and_7_out, and_8_out, and_9_out,
       clock_1_out, j_k_ff_1_q, j_k_ff_2_q, j_k_ff_3_q, j_k_ff_4_q, j_k_ff_4_qn, j_k_ff_5_q, j_k_ff_6_q,
       j_k_ff_7_q, j_k_ff_8_q, j_k_ff_8_qn, not_1_out, not_2_out, or_1_out, or_2_out;

  Clock clock_1 (.out(clock_1_out));
  J_K_Flip_Flop j_k_ff_1 (
    .J(in_1), .clk(clock_1_out), .K(in_1), .Q(j_k_ff_1_q), .reset(and_5_out));  // open: Qn, preset, en
  and and_1 (and_1_out, j_k_ff_1_q, j_k_ff_4_qn);
  J_K_Flip_Flop j_k_ff_2 (
    .J(and_1_out), .clk(clock_1_out), .K(and_1_out), .Q(j_k_ff_2_q), .reset(and_5_out));  // open: Qn, preset, en
  and and_2 (and_2_out, j_k_ff_1_q, j_k_ff_2_q);
  J_K_Flip_Flop j_k_ff_3 (
    .J(and_2_out), .clk(clock_1_out), .K(and_2_out), .Q(j_k_ff_3_q), .reset(and_5_out));  // open: Qn, preset, en
  and and_3 (and_3_out, j_k_ff_4_q, j_k_ff_1_q);
  and and_4 (and_4_out, j_k_ff_3_q, and_2_out);
  J_K_Flip_Flop j_k_ff_4 (
    .J(or_1_out), .clk(clock_1_out), .K(or_1_out), .Q(j_k_ff_4_q), .Qn(j_k_ff_4_qn), .reset(and_5_out));  // open: preset, en
  or or_1 (or_1_out, and_3_out, and_4_out);
  not not_1 (not_1_out, j_k_ff_2_q);
  not not_2 (not_2_out, j_k_ff_3_q);
  and and_5 (and_5_out, j_k_ff_1_q, not_1_out, not_2_out, j_k_ff_4_q);
  J_K_Flip_Flop j_k_ff_5 (
    .J(and_5_out), .clk(j_k_ff_4_qn), .K(and_5_out), .Q(j_k_ff_5_q));  // open: Qn, preset, en, reset
  and and_6 (and_6_out, j_k_ff_5_q, j_k_ff_8_qn);
  J_K_Flip_Flop j_k_ff_6 (
    .J(and_6_out), .clk(j_k_ff_4_qn), .K(and_6_out), .Q(j_k_ff_6_q));  // open: Qn, preset, en, reset
  and and_7 (and_7_out, j_k_ff_5_q, j_k_ff_6_q);
  J_K_Flip_Flop j_k_ff_7 (
    .J(and_7_out), .clk(j_k_ff_4_qn), .K(and_7_out), .Q(j_k_ff_7_q));  // open: Qn, preset, en, reset
  and and_8 (and_8_out, j_k_ff_8_q, j_k_ff_5_q);
  and and_9 (and_9_out, j_k_ff_7_q, and_7_out);
  or or_2 (or_2_out, and_8_out, and_9_out);
  J_K_Flip_Flop j_k_ff_8 (
    .J(or_2_out), .clk(j_k_ff_4_qn), .K(or_2_out), .Q(j_k_ff_8_q), .Qn(j_k_ff_8_qn));  // open: preset, en, reset
endmodule
